# Fritzing sketch blackpill (saved by Fritzing 1.0.0d)
breadboards: 1

parts:
  A1 = weact studio black pill
  U1 = ST7735 1.8 inch TFT LCD [package="SIP (Single Inline) [THT]"]

nets:
  N1: A1.Pin_1, A1.Pin_44, U1.VLED
  N2: A1.Pin_4, A1.Pin_43, U1.GND
  N3: A1.Pin_14, U1.CS
  N4: A1.Pin_15, U1.SCK
  N5: A1.Pin_17, U1.SDA
  N6: A1.Pin_18, U1.A0
  N7: A1.Pin_19, U1.RST
  N8: A1.Pin_24, A1.Pin_42, U1.VCC

custom parts:
  weact studio black pill: The STM32F401CE based Black Pill V3.0+ Board.
  ST7735 1.8 inch TFT LCD: 1.8 inch TFT LCD module. SPI interface, ST7735 controller
